# Fritzing sketch data sketch (saved by Fritzing 0.9.3b)

parts:
  Componente1 = Arduino Uno (Rev3)
  U1 = ESP8266 ESP-01 Upgraded WiFi Module [part_number=ESP8266]
  Raspberry_Pi1 = Raspberry Pi (Model B)
  GLCD_128x1 = 128 x 64 Graphic LCD  # not connected

nets:
  N1: Componente1.A4/SDA, Raspberry_Pi1.SDA
  N2: Componente1.A5/SCL, Raspberry_Pi1.SCL
  N3: Componente1.D2, U1.TXD
  N4: Componente1.D3_PWM, U1.RXD
  3V3: Componente1.3V3, U1.VCC, U1.CH_PD
  GND: Componente1.GND, U1.GND, Raspberry_Pi1.GND

custom parts:
  ESP8266 ESP-01 Upgraded WiFi Module: Upgraded Version ESP-01,all Flash are upgraded to 1M byte.Also support Cloud service remote transmission.
  Raspberry Pi (Model B): Raspberry Pi Single-board Computer, Model B
