# Fritzing sketch dp2 (saved by Fritzing 0.9.3b)
breadboards: 1

parts:
  U1 = ESP8266 ESP-01 Upgraded WiFi Module [part_number=ESP8266]
  YwRobot_Power_Supply1 = YwRobot Breadboard Power Supply [part_number=545043]
  Componente1 = Adafruit ADXL345 [part_number="Adafruit #1231"]
  LCD1 = LCD screen
  LCM1602_IIC2 = LCM1602 IIC [part_number="LCM1602 IIC" chip_label="LCM1602 IIC" package="DIP (Dual Inline) [THT]"]

nets:
  VCC: U1.VCC, U1.CH_PD, YwRobot_Power_Supply1.VCC#9, Componente1.3.3V, Componente1.CS, LCM1602_IIC2.VCC
  N1: U1.GPIO_0, Componente1.SDA/SDIO, LCM1602_IIC2.SDA
  N2: U1.GPIO_2, Componente1.SCL, LCM1602_IIC2.SCL
  GND: U1.GND, YwRobot_Power_Supply1.GND#13, Componente1.GND, LCM1602_IIC2.GND
  VSS: LCD1.VSS, LCM1602_IIC2.VSS
  VDD: LCD1.VDD, LCM1602_IIC2.VDD
  N3: LCD1.V0, LCM1602_IIC2.V0
  N4: LCD1.RS, LCM1602_IIC2.RS
  N5: LCD1.R/W, LCM1602_IIC2.RW
  N6: LCD1.E, LCM1602_IIC2.E
  N7: LCD1.DB0, LCM1602_IIC2.D0
  N8: LCD1.DB1, LCM1602_IIC2.D1
  N9: LCD1.DB2, LCM1602_IIC2.D2
  N10: LCD1.DB3, LCM1602_IIC2.D3
  N11: LCD1.DB4, LCM1602_IIC2.D4
  N12: LCD1.DB5, LCM1602_IIC2.D5
  N13: LCD1.DB6, LCM1602_IIC2.D6
  N14: LCD1.DB7, LCM1602_IIC2.D7
  N15: LCD1.LED+, LCM1602_IIC2.A
  N16: LCD1.LED-, LCM1602_IIC2.K

custom parts:
  ESP8266 ESP-01 Upgraded WiFi Module: Upgraded Version ESP-01,all Flash are upgraded to 1M byte.Also support Cloud service remote transmission.
  YwRobot Breadboard Power Supply: The YwRobot Breadboard Power Supply (MB-V2) has two power rails; they can be 5V or 3V3. Power to the module can be provided through the female USB socket or through the A10 (female) 2.1mm power jack.
  Adafruit ADXL345: Filling out our accelerometer offerings, we now have the really lovely digital ADXL345 from Analog Devices, a triple-axis accelerometer with digital I2C and SPI interface breakout. We added an on-board 3.3V regulator and logic-level shifting circuitry, making it a perfect choice for interfacing with any 3V or 5V microcontroller such as the Arduino. The sensor has three axes of measurements, X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
  LCM1602 IIC: I2C-Module to use a 1602 or 2004 LCD on with the wire.h libory Serial LCD Modul
