# Fritzing sketch MQTTesquema (saved by Fritzing 0.9.3b)
breadboards: 1

parts:
  IC1 = MCP23017 I2C I/O Expander
  LED1 = LED - 5mm [color="Red (633nm)" package="5 mm [THT]"]
  LED2 = LED - 5mm [color="Red (633nm)" package="5 mm [THT]"]
  LED3 = LED - 5mm [color="Red (633nm)" package="5 mm [THT]"]
  LED4 = LED - 5mm [color="Red (633nm)" package="5 mm [THT]"]
  LED5 = LED - 5mm [color="Red (633nm)" package="5 mm [THT]"]
  LED6 = LED - 5mm [color="Red (633nm)" package="5 mm [THT]"]
  LED7 = LED - 5mm [color="Red (633nm)" package="5 mm [THT]"]
  LED8 = LED - 5mm [color="Red (633nm)" package="5 mm [THT]"]
  U1 = ESP8266 NodeMCU LoLin module
  R1 = Resistor [tolerance=±5% resistance=220 package="0805 [SMD]"]

nets:
  N1: IC1.GPB0, LED1.anode
  N2: IC1.GPB1, LED2.anode
  N3: IC1.GPB2, LED3.anode
  N4: IC1.GPB3, LED4.anode
  N5: IC1.GPB4, LED5.anode
  N6: IC1.GPB5, LED6.anode
  N7: IC1.GPB6, LED7.anode
  N8: IC1.GPB7, LED8.anode
  N9: IC1.SCL, U1.D1
  N10: IC1.SDA, U1.D2
  N11: IC1.A0, IC1.A1, IC1.A2, LED1.cathode, LED2.cathode, LED3.cathode, LED4.cathode, LED5.cathode, LED6.cathode, LED7.cathode, LED8.cathode, U1.GND
  N12: IC1.RESET, R1.Pin_0
  N13: U1.3V3, R1.Pin_1

custom parts:
  MCP23017 I2C I/O Expander: The MCP23017 uses two i2c pins (these can be shared with other i2c devices), and in exchange gives you 16 general purpose pins. You can set each of 16 pins to be input, output, input with a pullup or open drain. There's even the ability to get an interrupt via an external pin when any of the inputs change so you don't have to keep polling the chip.
  ESP8266 NodeMCU LoLin module: ESP8266 based NodeMCU
